// Logisim project MicroProcesserCirc2.circ as structural Verilog: 7 circuits, main circuit ALU
module RF (
  input  [3:0] DI,
  input  [2:0] DA,
  input  WR,
  input  [2:0] AA,
  input  RESET,
  input  [2:0] BA,
  input  CLK,
  output [3:0] AO,
  output [3:0] BO
);

  wire demultiplexer_1_out0, demultiplexer_1_out1, demultiplexer_1_out2, demultiplexer_1_out3,
       demultiplexer_1_out4, demultiplexer_1_out5, demultiplexer_1_out6, demultiplexer_1_out7;
  wire [3:0] demultiplexer_2_out0, demultiplexer_2_out1, demultiplexer_2_out2, demultiplexer_2_out3,
       demultiplexer_2_out4, demultiplexer_2_out5, demultiplexer_2_out6, demultiplexer_2_out7, register_1_q,
       register_2_q, register_3_q, register_4_q, register_5_q, register_6_q, register_7_q, register_8_q;

  Demultiplexer #(.select(3), .enable("false")) demultiplexer_1 (
    .out0(demultiplexer_1_out0), .out1(demultiplexer_1_out1), .out2(demultiplexer_1_out2),
    .out3(demultiplexer_1_out3), .out4(demultiplexer_1_out4), .out5(demultiplexer_1_out5),
    .out6(demultiplexer_1_out6), .out7(demultiplexer_1_out7), .in(WR), .sel(DA));
  Demultiplexer #(.select(3), .width(4), .enable("false")) demultiplexer_2 (
    .out0(demultiplexer_2_out0), .out1(demultiplexer_2_out1), .out2(demultiplexer_2_out2),
    .out3(demultiplexer_2_out3), .out4(demultiplexer_2_out4), .out5(demultiplexer_2_out5),
    .out6(demultiplexer_2_out6), .out7(demultiplexer_2_out7), .in(DI), .sel(DA));
  Register #(.width(4)) register_1 (
    .D(demultiplexer_2_out0), .en(demultiplexer_1_out0), .Q(register_1_q), .clk(CLK), .clr(RESET));
  Register #(.width(4)) register_2 (
    .D(demultiplexer_2_out2), .en(demultiplexer_1_out2), .Q(register_2_q), .clk(CLK), .clr(RESET));
  Register #(.width(4)) register_3 (
    .D(demultiplexer_2_out4), .en(demultiplexer_1_out4), .Q(register_3_q), .clk(CLK), .clr(RESET));
  Register #(.width(4)) register_4 (
    .D(demultiplexer_2_out6), .en(demultiplexer_1_out6), .Q(register_4_q), .clk(CLK), .clr(RESET));
  Register #(.width(4)) register_5 (
    .D(demultiplexer_2_out1), .en(demultiplexer_1_out1), .Q(register_5_q), .clk(CLK), .clr(RESET));
  Register #(.width(4)) register_6 (
    .D(demultiplexer_2_out3), .en(demultiplexer_1_out3), .Q(register_6_q), .clk(CLK), .clr(RESET));
  Register #(.width(4)) register_7 (
    .D(demultiplexer_2_out5), .en(demultiplexer_1_out5), .Q(register_7_q), .clk(CLK), .clr(RESET));
  Register #(.width(4)) register_8 (
    .D(demultiplexer_2_out7), .en(demultiplexer_1_out7), .Q(register_8_q), .clk(CLK), .clr(RESET));
  Multiplexer #(.select(3), .width(4), .enable("false")) multiplexer_1 (
    .in0(register_1_q), .in1(register_5_q), .in2(register_2_q), .in3(register_6_q), .in4(register_3_q),
    .in5(register_7_q), .in6(register_4_q), .in7(register_8_q), .out(AO), .sel(AA));
  Multiplexer #(.select(3), .width(4), .enable("false")) multiplexer_2 (
    .in0(register_1_q), .in1(register_5_q), .in2(register_2_q), .in3(register_6_q), .in4(register_3_q),
    .in5(register_7_q), .in6(register_4_q), .in7(register_8_q), .out(BO), .sel(BA));

  // Notes on the sheet:
  //   Register File
endmodule

module CAR (
  input  MODE,
  input  [7:0] J_ADDR,
  input  CLK,
  input  RESET,
  output [7:0] NEXT_ADDR,
  output READY
);

  wire not_1_out;

  not not_1 (not_1_out, MODE);
  Counter NEXT_ADR (.load(MODE), .D(J_ADDR), .count(not_1_out), .Q(NEXT_ADDR), .clk(CLK), .clr(RESET));  // open: carry
  Comparator comparator_1 (.a(NEXT_ADDR), .b({8{1'b0}}), .eq(READY));  // open: gt, lt

  // Notes on the sheet:
  //   J_ADDR = jump address
  //   Address Counter.
  //   When Mode = 1, loads J_ADDR into the Counter
  //   When Mode = 0, counter increments the loaded value
  //   Ready indicates that the processor is ready to execute the next input instruction
  //   Therefore, it is only ready when address = 0x00, the start address in ROM
endmodule

// BL
module BRA_LOG (
  input  [2:0] COND,
  input  [2:0] PZN,
  output BRA
);

  wire or_1_out, or_2_out, or_3_out;

  or or_1 (or_1_out, PZN[1], PZN[0]);
  or or_2 (or_2_out, PZN[2], PZN[0]);
  or or_3 (or_3_out, PZN[2], PZN[1]);
  Multiplexer #(.select(3), .enable("false")) multiplexer_1 (
    .in0(1'b0), .in1(PZN[0]), .in2(PZN[1]), .in3(or_1_out), .in4(PZN[2]), .in5(or_2_out), .in6(or_3_out),
    .in7(1'b1), .out(BRA), .sel(COND));
endmodule

module FU (
  input  [3:0] ValM_A,
  input  [3:0] C,
  input  [3:0] OPCODE,
  output [3:0] OUT,
  output [2:0] PZN
);

  wire comparator_1_eq, comparator_2_eq;
  wire [3:0] adder_1_out, and_1_out, multiplexer_1_out, multiplexer_2_out, multiplier_1_out, not_1_out,
       shifter_1_out, subtractor_1_out;

  Adder #(.width(4)) adder_1 (.a(ValM_A), .b(C), .out(adder_1_out));  // open: cin, cout
  Subtractor #(.width(4)) subtractor_1 (.a(ValM_A), .b(C), .out(subtractor_1_out));  // open: bin, bout
  Multiplier #(.width(4)) multiplier_1 (.a(ValM_A), .b(C), .out(multiplier_1_out));  // open: cin, cout
  Shifter #(.width(4), .shift("lr")) shifter_1 (.in(ValM_A), .\dist (2'b01), .out(shifter_1_out));
  assign not_1_out = ~ValM_A;  // NOT_Gate not_1, 4 bits wide
  assign and_1_out = ValM_A & C;  // AND_Gate and_1, 4 bits wide
  Comparator #(.width(4)) comparator_1 (.a(4'b0000), .b(C), .eq(comparator_1_eq));  // open: gt, lt
  Comparator #(.width(4)) comparator_2 (.a(ValM_A), .b(C), .eq(comparator_2_eq));  // open: gt, lt
  Multiplexer #(.width(4), .enable("false")) multiplexer_1 (
    .in0(4'b0001), .in1(4'b0000), .out(multiplexer_1_out), .sel(comparator_2_eq));
  Multiplexer #(.width(4), .enable("false")) multiplexer_2 (
    .in1(ValM_A), .out(multiplexer_2_out), .sel(comparator_1_eq));  // open: in0
  Multiplexer #(.select(4), .width(4), .enable("false")) multiplexer_3 (
    .in1(ValM_A), .in2(C), .in3(adder_1_out), .in4(subtractor_1_out), .in5(multiplier_1_out),
    .in6(shifter_1_out), .in7(not_1_out), .in8(and_1_out), .in9(multiplexer_2_out), .in10(multiplexer_1_out),
    .out(OUT), .sel(OPCODE));  // open: in0, in11, in12, in13, in14, in15
  Comparator #(.width(4)) comparator_3 (.a(OUT), .b(4'b0000), .gt(PZN[0]), .eq(PZN[1]), .lt(PZN[2]));
endmodule

module CU (
  input  [13:0] INST,
  input  START,
  input  CLK,
  input  RESET,
  input  [2:0] PZN,
  output [2:0] D,
  output [3:0] C,
  output [2:0] A,
  output [6:0] CW,
  output MW,
  output READY
);

  wire bra_log_1_bra, or_1_out;
  wire [2:0] demultiplexer_1_out1, register_4_q;
  wire [7:0] car_1_next_addr, demultiplexer_1_out1_2, multiplexer_1_out, rom_1_data;
  wire [10:8] demultiplexer_1_out0;
  wire [11:0] rom_2_data;

  or or_1 (or_1_out, START, bra_log_1_bra);
  Multiplexer #(.width(8), .enable("false")) multiplexer_1 (
    .in0(demultiplexer_1_out1_2), .in1(rom_1_data), .out(multiplexer_1_out), .sel(START));
  CAR car_1 (
    .MODE(or_1_out), .J_ADDR(multiplexer_1_out), .CLK(CLK), .RESET(RESET), .NEXT_ADDR(car_1_next_addr),
    .READY(READY));
  ROM #(.addrWidth(4)) rom_1 (.addr(INST[13:10]), .data(rom_1_data));  // open: sel
  BRA_LOG bra_log_1 (.COND(demultiplexer_1_out1), .PZN(register_4_q), .BRA(bra_log_1_bra));
  ROM #(.dataWidth(12)) rom_2 (.addr(car_1_next_addr), .data(rom_2_data));  // open: sel
  Register #(.width(3)) register_1 (.D(INST[2:0]), .en(1'b1), .Q(D), .clk(CLK), .clr(RESET));
  Register #(.width(4)) register_2 (.D(INST[6:3]), .en(1'b1), .Q(C), .clk(CLK), .clr(RESET));
  Register #(.width(3)) register_3 (.D(INST[9:7]), .en(1'b1), .Q(A), .clk(CLK), .clr(RESET));
  Demultiplexer #(.width(11), .enable("false")) demultiplexer_1 (
    .out0({demultiplexer_1_out0, MW, CW}), .out1({demultiplexer_1_out1_2, demultiplexer_1_out1}),
    .in(rom_2_data[10:0]), .sel(rom_2_data[11]));
  Register #(.width(3)) register_4 (.D(PZN), .Q(register_4_q), .clk(CLK), .clr(RESET));  // open: en

  // Notes on the sheet:
  //   contents of rom_1 (hex, n*v repeats v):
  //   0 10 20 30 40 50 60 70 80 90 a0 b0 c0 d0 e0 f0
  //   contents of rom_2 (hex, n*v repeats v):
  //   16*0 221 400 14*0 221 423 103 220 12*0 221 423 625 303 105 433 200 9*0 221 423 625 303 105 443 200
  //   9*0 221 423 625 303 105 453 200 9*0 221 423 303 63 200 11*0 221 423 303 73 200 11*0 221 423 625 303
  //   105 483 200 9*0 625 105 420 0 221 423 103 200 8*0 221 423 625 103 105 4a3 200
endmodule

// DU
module ALU (
  input  [2:0] D,
  input  [2:0] A,
  input  RESET,
  input  [3:0] C,
  input  CLK,
  input  [3:0] Data_From_Memory,
  input  [6:0] FULL_CONWORD,
  output [3:0] AddressOut,
  output [3:0] Data_Out,
  output [2:0] PZN
);

  wire not_1_out;
  wire [3:0] fu_1_out, multiplexer_2_out, rf_1_bo;

  not not_1 (not_1_out, FULL_CONWORD[2]);
  RF rf_1 (
    .DI(multiplexer_2_out), .DA(D), .WR(FULL_CONWORD[0]), .AA(A), .RESET(RESET), .BA(C[2:0]), .CLK(CLK),
    .AO(AddressOut), .BO(rf_1_bo));
  Multiplexer #(.width(4), .enable("false")) multiplexer_1 (.in0(C), .in1(rf_1_bo), .out(Data_Out), .sel(not_1_out));
  FU fu_1 (.ValM_A(AddressOut), .C(Data_Out), .OPCODE(FULL_CONWORD[6:3]), .OUT(fu_1_out), .PZN(PZN));
  Multiplexer #(.width(4), .enable("false")) multiplexer_2 (
    .in0(fu_1_out), .in1(Data_From_Memory), .out(multiplexer_2_out), .sel(FULL_CONWORD[1]));

  // Notes on the sheet:
  //   operandMuxToFU
  //   Data From Memory?
  //   PZN_OUT
  //   regToMux_opB
  //   FUResultToMux
  //   regToMux_OpA
  //   muxToRegisterFileDest
  //   DATA PATH
  //   15:13 AA
  //   12 BO
  //   11:9 BA
  //   8 DFM
  //   7:4 OPCODE
  //   3:1 DA
  //   0 WR
  //   A Address
  //   B as Constant or From Memory
  //   B Address
  //   Data From Memory(?)
  //   Operation Code
  //   Data Address (where to write)
  //   Read Or write data
endmodule

module PROC (
  input  [13:0] INSTRUCTION,
  input  START,
  input  RESET
);

  wire and_1_out, CLK_out, cu_1_mw, cu_1_ready, not_1_out;
  wire [2:0] alu_1_pzn, cu_1_a, cu_1_d;
  wire [3:0] alu_1_addressout, alu_1_data_out, cu_1_c, ram_1_data;
  wire [6:0] cu_1_cw;

  Clock CLK (.out(CLK_out));
  and and_1 (and_1_out, START, cu_1_ready);
  CU cu_1 (
    .INST(INSTRUCTION), .START(and_1_out), .CLK(CLK_out), .RESET(RESET), .D(cu_1_d), .C(cu_1_c), .A(cu_1_a),
    .CW(cu_1_cw), .MW(cu_1_mw), .PZN(alu_1_pzn), .READY(cu_1_ready));
  ALU alu_1 (
    .D(cu_1_d), .A(cu_1_a), .RESET(RESET), .C(cu_1_c), .CLK(CLK_out), .FULL_CONWORD(cu_1_cw),
    .PZN(alu_1_pzn), .AddressOut(alu_1_addressout), .Data_Out(alu_1_data_out), .Data_From_Memory(ram_1_data));
  not not_1 (not_1_out, cu_1_mw);
  RAM #(.addrWidth(4), .dataWidth(4), .bus("separate")) ram_1 (
    .addr(alu_1_addressout), .din(alu_1_data_out), .data(ram_1_data), .str(cu_1_mw), .clk(CLK_out),
    .ld(not_1_out), .clr(RESET));  // open: sel

  // Notes on the sheet:
  //   READY
  //   Topview of the Processor
  //   INSTRUCTION is fed into the CPU to be executed
  //   DU is the datapath
  //   RAM in included for data storage
  //   The CPU will only take an instruction if both START and READY are 1
endmodule
