// Logisim project MicroProcesserCirc_3.circ as structural Verilog: 8 circuits, main circuit ALU
module RF (
  input  [7:0] DI,
  input  [2:0] DA,
  input  WR,
  input  [2:0] AA,
  input  RESET,
  input  [2:0] BA,
  input  CLK,
  output [7:0] AO,
  output [7:0] BO
);

  wire demultiplexer_1_out1, demultiplexer_1_out2, demultiplexer_1_out3, demultiplexer_1_out4,
       demultiplexer_1_out5, demultiplexer_1_out6, demultiplexer_1_out7;
  wire [7:0] demultiplexer_2_out1, demultiplexer_2_out2, demultiplexer_2_out3, demultiplexer_2_out4,
       demultiplexer_2_out5, demultiplexer_2_out6, demultiplexer_2_out7, register_1_q, register_2_q,
       register_3_q, register_4_q, register_5_q, register_6_q, register_7_q, register_8_q;

  Demultiplexer #(.select(3), .enable("false")) demultiplexer_1 (
    .out1(demultiplexer_1_out1), .out2(demultiplexer_1_out2), .out3(demultiplexer_1_out3),
    .out4(demultiplexer_1_out4), .out5(demultiplexer_1_out5), .out6(demultiplexer_1_out6),
    .out7(demultiplexer_1_out7), .in(WR), .sel(DA));  // open: out0
  Demultiplexer #(.select(3), .width(8), .enable("false")) demultiplexer_2 (
    .out1(demultiplexer_2_out1), .out2(demultiplexer_2_out2), .out3(demultiplexer_2_out3),
    .out4(demultiplexer_2_out4), .out5(demultiplexer_2_out5), .out6(demultiplexer_2_out6),
    .out7(demultiplexer_2_out7), .in(DI), .sel(DA));  // open: out0
  Register register_1 (.en(1'b0), .Q(register_1_q), .clk(CLK), .clr(RESET));  // open: D
  Register register_2 (.D(demultiplexer_2_out2), .en(demultiplexer_1_out2), .Q(register_2_q), .clk(CLK), .clr(RESET));
  Register register_3 (.D(demultiplexer_2_out4), .en(demultiplexer_1_out4), .Q(register_3_q), .clk(CLK), .clr(RESET));
  Register register_4 (.D(demultiplexer_2_out6), .en(demultiplexer_1_out6), .Q(register_4_q), .clk(CLK), .clr(RESET));
  Register register_5 (.D(demultiplexer_2_out1), .en(demultiplexer_1_out1), .Q(register_5_q), .clk(CLK), .clr(RESET));
  Register register_6 (.D(demultiplexer_2_out3), .en(demultiplexer_1_out3), .Q(register_6_q), .clk(CLK), .clr(RESET));
  Register register_7 (.D(demultiplexer_2_out5), .en(demultiplexer_1_out5), .Q(register_7_q), .clk(CLK), .clr(RESET));
  Register register_8 (.D(demultiplexer_2_out7), .en(demultiplexer_1_out7), .Q(register_8_q), .clk(CLK), .clr(RESET));
  Multiplexer #(.select(3), .width(8), .enable("false")) multiplexer_1 (
    .in0(register_1_q), .in1(register_5_q), .in2(register_2_q), .in3(register_6_q), .in4(register_3_q),
    .in5(register_7_q), .in6(register_4_q), .in7(register_8_q), .out(AO), .sel(AA));
  Multiplexer #(.select(3), .width(8), .enable("false")) multiplexer_2 (
    .in0(register_1_q), .in1(register_5_q), .in2(register_2_q), .in3(register_6_q), .in4(register_3_q),
    .in5(register_7_q), .in6(register_4_q), .in7(register_8_q), .out(BO), .sel(BA));

  // Notes on the sheet:
  //   Register File
endmodule

module CAR (
  input  MODE,
  input  [7:0] J_ADDR,
  input  CLK,
  input  RESET,
  output [7:0] NEXT_ADDR,
  output READY
);

  wire not_1_out;

  not not_1 (not_1_out, MODE);
  Counter NEXT_ADR (.load(MODE), .D(J_ADDR), .count(not_1_out), .Q(NEXT_ADDR), .clk(CLK), .clr(RESET));  // open: carry
  Comparator comparator_1 (.a(NEXT_ADDR), .b({8{1'b0}}), .eq(READY));  // open: gt, lt

  // Notes on the sheet:
  //   J_ADDR = jump address
  //   Address Counter.
  //   When Mode = 1, loads J_ADDR into the Counter
  //   When Mode = 0, counter increments the loaded value
  //   Ready indicates that the processor is ready to execute the next input instruction
  //   Therefore, it is only ready when address = 0x00, the start address in ROM
endmodule

// BL
module BRA_LOG (
  input  [2:0] COND,
  input  [2:0] PZN,
  output BRA
);

  wire or_1_out, or_2_out, or_3_out;

  or or_1 (or_1_out, PZN[1], PZN[0]);
  or or_2 (or_2_out, PZN[2], PZN[0]);
  or or_3 (or_3_out, PZN[2], PZN[1]);
  Multiplexer #(.select(3), .enable("false")) multiplexer_1 (
    .in0(1'b0), .in1(PZN[0]), .in2(PZN[1]), .in3(or_1_out), .in4(PZN[2]), .in5(or_2_out), .in6(or_3_out),
    .in7(1'b1), .out(BRA), .sel(COND));
endmodule

module FU (
  input  [7:0] ValM_A,
  input  [7:0] C,
  input  [3:0] OPCODE,
  output [7:0] OUT,
  output [2:0] PZN
);

  wire comparator_1_eq, comparator_2_eq;
  wire [7:0] adder_1_out, and_1_out, multiplexer_1_out, multiplexer_2_out, not_1_out, shifter_1_out,
       subtractor_1_out;

  Adder adder_1 (.a(ValM_A), .b(C), .out(adder_1_out));  // open: cin, cout
  Subtractor subtractor_1 (.a(ValM_A), .b(C), .out(subtractor_1_out));  // open: bin, bout
  Multiplier multiplier_1 (.a(ValM_A), .b(C));  // open: out, cin, cout
  Shifter #(.shift("lr")) shifter_1 (.in(ValM_A), .\dist (3'b001), .out(shifter_1_out));
  assign not_1_out = ~ValM_A;  // NOT_Gate not_1, 8 bits wide
  assign and_1_out = ValM_A & C;  // AND_Gate and_1, 8 bits wide
  Comparator comparator_1 (.a({8{1'b0}}), .b(C), .eq(comparator_1_eq));  // open: gt, lt
  Comparator comparator_2 (.a(ValM_A), .b(C), .eq(comparator_2_eq));  // open: gt, lt
  Multiplexer #(.width(8), .enable("false")) multiplexer_1 (
    .in0({8{1'b0}}), .in1(ValM_A), .out(multiplexer_1_out), .sel(comparator_1_eq));
  Multiplexer #(.width(8), .enable("false")) multiplexer_2 (
    .in0({8{1'b0}}), .in1(8'h1), .out(multiplexer_2_out), .sel(comparator_2_eq));
  Multiplexer #(.select(4), .width(8), .enable("false")) multiplexer_3 (
    .in0(ValM_A), .in1(C), .in2(adder_1_out), .in3(subtractor_1_out), .in4(shifter_1_out), .in5(not_1_out),
    .in6(and_1_out), .in7(multiplexer_1_out), .in8(multiplexer_2_out), .out(OUT), .sel(OPCODE));  // open: in9, in10, in11, in12, in13, in14, in15
  Comparator comparator_3 (.a(OUT), .b({8{1'b0}}), .gt(PZN[0]), .eq(PZN[1]), .lt(PZN[2]));

  // Notes on the sheet:
  //   Control Word Bits [6:0]
  //   6:3 = OPCODE
  //   2 = const (1) or register (0)
  //   1 = data from FU (0), data from ram (1)
  //   0 = isWrite
endmodule

module CU (
  input  [17:0] INST,
  input  RESET,
  input  CLK,
  output [2:0] D,
  output [7:0] C,
  output [2:0] A,
  output [6:0] CW,
  output MW,
  output [2:0] CON,
  output [7:0] Branch
);

  wire [11:0] rom_1_data;
  wire [11:11] register_1_q;

  ROM #(.addrWidth(4), .dataWidth(12)) rom_1 (.addr(INST[17:14]), .data(rom_1_data));  // open: sel
  Register #(.width(12)) register_1 (
    .D(rom_1_data), .en(1'b1), .Q({register_1_q[11], Branch, CON}), .clk(CLK), .clr(RESET));
  Register #(.width(3)) register_2 (.D(INST[2:0]), .en(1'b1), .Q(D), .clk(CLK), .clr(RESET));
  Register register_3 (.D(INST[10:3]), .en(1'b1), .Q(C), .clk(CLK), .clr(RESET));
  Register #(.width(3)) register_4 (.D(INST[13:11]), .en(1'b1), .Q(A), .clk(CLK), .clr(RESET));

  assign CW = {Branch[3:0], CON};
  assign MW = Branch[4];

  // Notes on the sheet:
  //   Control Word Bits [6:0]
  //   6:3 = OPCODE
  //   0 = isWrite
  //   2 = const (1) or register (0)
  //   1 = data from FU (0), data from ram (1)
  //   contents of rom_1 (hex, n*v repeats v):
  //   0 d 13 1 80 11 15 1d 19 21 29 31 7 45 41 84
  //   Send to PC for jumps
endmodule

// DU
module ALU (
  input  [2:0] D,
  input  [2:0] A,
  input  RESET,
  input  [7:0] C,
  input  CLK,
  input  [7:0] Data_From_Memory,
  input  [6:0] FULL_CONWORD,
  output [7:0] AddressOut,
  output [7:0] Data_Out,
  output [2:0] PZN
);

  wire not_1_out;
  wire [7:0] fu_1_out, multiplexer_2_out, rf_1_bo;

  not not_1 (not_1_out, FULL_CONWORD[2]);
  Multiplexer #(.width(8), .enable("false")) multiplexer_1 (.in0(C), .in1(rf_1_bo), .out(AddressOut), .sel(not_1_out));
  FU fu_1 (.ValM_A(Data_Out), .C(AddressOut), .OPCODE(FULL_CONWORD[6:3]), .OUT(fu_1_out), .PZN(PZN));
  RF rf_1 (
    .DI(multiplexer_2_out), .DA(D), .WR(FULL_CONWORD[0]), .AA(A), .RESET(RESET), .BA(C[2:0]), .CLK(CLK),
    .AO(Data_Out), .BO(rf_1_bo));
  Multiplexer #(.width(8), .enable("false")) multiplexer_2 (
    .in0(fu_1_out), .in1(Data_From_Memory), .out(multiplexer_2_out), .sel(FULL_CONWORD[1]));

  // Notes on the sheet:
  //   operandMuxToFU
  //   Data From Memory?
  //   regToMux_opB
  //   PZN_OUT
  //   regToMux_OpA
  //   FUResultToMux
  //   DATA PATH
  //   muxToRegisterFileDest
  //   Control Word Bits [6:0]
  //   6:3 = OPCODE
  //   2 = const (1) or register (0)
  //   0 = isWrite
  //   1 = data from FU (0), data from ram (1)
endmodule

module PROC (
  input  START,
  input  RESET
);

  wire CLK_out, cu_1_mw, not_1_out;
  wire [2:0] alu_1_pzn, cu_1_a, cu_1_con, cu_1_d;
  wire [6:0] cu_1_cw;
  wire [7:0] alu_1_addressout, alu_1_data_out, counter_1_q, cu_1_branch, cu_1_c, ram_1_data;
  wire [17:0] rom_1_data;

  Counter counter_1 (.count(1'b1), .Q(counter_1_q), .clk(CLK_out), .clr(RESET));  // open: load, D, carry
  ROM #(.dataWidth(18)) rom_1 (.addr(counter_1_q), .data(rom_1_data));  // open: sel
  Clock CLK (.out(CLK_out));
  CU cu_1 (
    .INST(rom_1_data), .RESET(RESET), .CLK(CLK_out), .D(cu_1_d), .C(cu_1_c), .A(cu_1_a), .CW(cu_1_cw),
    .MW(cu_1_mw), .CON(cu_1_con), .Branch(cu_1_branch));
  PC pc_1 (
    .CLK(CLK_out), .RESET(RESET), .CON(cu_1_con), .PZN(alu_1_pzn), .BRANCH_ADDR(cu_1_branch));  // open: READY, NEXT_INST_ADDR
  ALU alu_1 (
    .D(cu_1_d), .A(cu_1_a), .RESET(RESET), .C(cu_1_c), .CLK(CLK_out), .FULL_CONWORD(cu_1_cw),
    .PZN(alu_1_pzn), .AddressOut(alu_1_addressout), .Data_Out(alu_1_data_out), .Data_From_Memory(ram_1_data));
  not not_1 (not_1_out, cu_1_mw);
  RAM #(.bus("separate")) ram_1 (
    .addr(alu_1_addressout), .din(alu_1_data_out), .data(ram_1_data), .str(cu_1_mw), .sel(1'b1),
    .clk(CLK_out), .ld(not_1_out));  // open: clr

  // Notes on the sheet:
  //   contents of rom_1 (hex, n*v repeats v):
  //   0 4011 401a 4023 402c 4035 403e 4047 1680a 1503b 1a054 21811 1f07d 26004 29006 2c81d 10820 f007 8023
  //   3003a
  //   Topview of the Processor
  //   INSTRUCTION is fed into the ControlUnit to be executed
  //   DU is the datapath
  //   RAM in included for data storage
  //   The CPU will only take an instruction if both START and READY are 1
endmodule

module PC (
  input  CLK,
  input  RESET,
  input  [2:0] CON,
  input  [2:0] PZN,
  input  [7:0] BRANCH_ADDR,
  output READY,
  output [7:0] NEXT_INST_ADDR
);

  wire bra_log_1_bra;

  CAR car_1 (
    .MODE(bra_log_1_bra), .J_ADDR(BRANCH_ADDR), .CLK(CLK), .RESET(RESET), .NEXT_ADDR(NEXT_INST_ADDR),
    .READY(READY));
  BRA_LOG bra_log_1 (.COND(CON), .PZN(PZN), .BRA(bra_log_1_bra));

  // Notes on the sheet:
  //   PZN: pull=down
endmodule
